// Digital circuit 3.3 Chip.dig as structural Verilog
module _3_3_Chip (
  input  D,
  input  C,
  input  B,
  input  A,
  output Y
);

  wire _7404_1_pin2, _7404_1_pin4, _7404_1_pin6, _7404_1_pin9, _7404_1_pin11, _7404_1_pin12;

  _7404 _7404_1 (
    .pin1(D), .pin2(_7404_1_pin2), .pin3(D), .pin4(_7404_1_pin4), .pin5(D), .pin6(_7404_1_pin6), .pin7(1'b0),
    .pin9(_7404_1_pin9), .pin11(_7404_1_pin11), .pin12(_7404_1_pin12), .pin13(D), .pin14(1'b1));  // open: pin8, pin10
  // NotConnected on _7404_1_pin11
  // NotConnected on _7404_1_pin9
  _74151 _74151_1 (
    .pin1(D), .pin2(D), .pin3(D), .pin4(D), .pin5(Y), .pin7(1'b0), .pin8(1'b0), .pin9(A), .pin10(B),
    .pin11(C), .pin12(_7404_1_pin12), .pin13(_7404_1_pin4), .pin14(_7404_1_pin2), .pin15(_7404_1_pin6),
    .pin16(1'b1));  // open: pin6
endmodule

/* Test case:
D	C	B	A	Y
0	0	0	0	0
1	0	0	0	1
0	1	0	0	0
1	1	0	0	1
0	0	1	0	0
1	0	1	0	1
0	1	1	0	0
1	1	1	0	X
0	0	0	1	1
1	0	0	1	0
0	1	0	1	1
1	1	0	1	X
0	0	1	1	1
1	0	1	1	0
0	1	1	1	1
1	1	1	1	X
*/
